# Fritzing sketch sensor-device1 (saved by Fritzing 0.9.3b)

parts:
  JL012-13-5_1 = JL012-13-5.2 Lever (Limit) Switch SPDT + NO + NC [part_number=JL012-13-5.2]
  U1 = POT [package=alps_pot]
  Mod1 = KY-019 5V Relay Module [package="Breakout board"]
  Mod2 = KY-019 5V Relay Module [package="Breakout board"]
  Mod3 = KY-019 5V Relay Module [package="Breakout board"]
  Mod4 = KY-019 5V Relay Module [package="Breakout board"]
  Mod5 = KY-019 5V Relay Module [package="Breakout board"]
  Mod6 = KY-019 5V Relay Module [package="Breakout board"]
  M1 = BTS7960
  M2 = DOIT Esp32 DevKit v1 (30 pins long, 11 pins width) [part_number=ESP32S-PIN30]
  M3 = DOIT Esp32 DevKit v1 (30 pins long, 11 pins width) [part_number=ESP32S-PIN30]
  M4 = Pzem-004t
  S1 = PH meter [package=THT]
  M5 = DFR sen0308 [package=THT]
  M6 = Pzem-004t
  M7 = Pzem-004t
  M8 = Pzem-004t
  M9 = Pzem-004t
  M10 = Pzem-004t
  M11 = DC Motor
  BULB1 = Incandescent light bulb small [package="bulb sm"]
  Raspberry_Pi_1 = Raspberry Pi 4 [part_number=RPI-4-b]  # not connected
  A1 = Arducam Multi Camera Adapter Module  # not connected
  IC1 = Rasberry Pi NIOR Camera [chip_label=IC package="DIP (Dual Inline) [THT]"]  # not connected
  IC2 = Rasberry Pi NIOR Camera [chip_label=IC package="DIP (Dual Inline) [THT]"]  # not connected
  IC3 = Rasberry Pi NIOR Camera [chip_label=IC package="DIP (Dual Inline) [THT]"]  # not connected
  Part1 = Adafruit BMP388 [part_number="Adafruit #3966"]
  Part2 = Adafruit SCD4x [part_number="Adafruit #5187"]  # not connected
  Part3 = TM1637  # not connected
  U2 = LM2596 step down module
  J1 = 120V duplex outlet_1
  J2 = 120V duplex outlet_1
  J3 = 120V duplex outlet_1
  Part4 = INA 260

nets:
  N1: JL012-13-5_1.NO, M2.D12
  N2: U1.S, M2.D13
  N3: Mod1.S, M3.D5
  N4: Mod1.NO, M9.LIN
  N5: Mod2.S, M3.D15
  N6: Mod3.S, M3.D23
  N7: Mod3.NO, M8.LIN
  N8: Mod4.S, M2.D23
  N9: Mod4.NO, M7.LIN
  N10: Mod5.S, M2.D19
  N11: Mod6.S, M2.D4
  N12: Mod6.NO, M4.LIN
  N13: M1.pin1, M2.D26
  N14: M1.pin2, M2.D27
  N15: M1.pin3, M2.D2
  N16: M1.pin9, M11.pin_2
  N17: M1.pin10, M11.pin_1
  N18: M2.RX2, M4.TX
  N19: M2.TX2, M4.RX
  N20: M2.D5, M6.TX
  N21: M2.D18, M6.RX
  N22: M2.D21, Part4.SDA
  N23: M2.D22, Part4.SCL
  N24: M2.D33, M7.RX
  N25: M2.D25, M7.TX
  GND: M2.GND, M3.GND, M5.pin1, M5.pin3
  VIN: M2.VIN, M3.VIN, M5.pin4
  N26: M3.D2, M10.TX
  N27: M3.D4, M10.RX
  N28: M3.RX2, M9.TX
  N29: M3.TX2, M9.RX
  N30: M3.D21, Part1.SDI/SDA
  N31: M3.RX0, M8.TX
  N32: M3.TX0, M8.RX
  N33: M3.D22, Part1.SCK/SCL
  N34: M3.D33, S1.pin1
  N35: M3.D25, M5.pin2
  N36: M10.LOUT, BULB1.1
  N37: U2.IN-, U2.OUT-
  N38: J1.H2, J2.N2
  N39: J2.H2, J3.N2

notes:
  BMP388
  ESP32
  pH Meter
  DHT22
  CO2 Sensor
  Soil Moisture & Humidity
  L
  N
  AC 220V
  INPUT
  LIMIT SWITCH
  DC to DC Converter
  Rotary Potentiometer
  SCD 41
  Relay
  PZEM-004T
  Power Socket
  Lighting System
  CT Coil
  BTS9760
  SMPS
  INA260

custom parts:
  JL012-13-5.2 Lever (Limit) Switch SPDT + NO + NC: Micro Switch; Model No.: JL012-13.5-2; Actuator Action: Momentary; Actuator Type: Hinge Lever; Contact Configuration: 1NO, 1NC (SPDT) Temperature -25~65℃；Relative humidity: below 85%; Rate Voltage: 125V AC; Rated Current: 1A.
  KY-019 5V Relay Module: KY-019 5V Relay module, used to control AC circuits. (Special thanks to vanepp for fixing the PCB holes and other errors)
  BTS7960: BTS7960 43A Peak Power H-Bridge PWM Motor Driver
  DOIT Esp32 DevKit v1 (30 pins long, 11 pins width): The DOIT Esp32 DevKit v1 is one of the development board created by DOIT to evaluate the ESP-WROOM-32 module. It is based on the ESP32 microcontroller that boasts Wifi, Bluetooth, Ethernet and Low Power support all in a single chip. (vanepp) made breadboard work, adjusted pin numbering and labels and reduced size of schematic and cleaned up pcb. This chip is 30pins long (2 x15) and 11 pins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
  Pzem-004t: Pzem-004t used for measuring AC voltage, current, active power, frequency, power factor and active energy, the module is without display function, the data is read through the TTL interface.
  DFR sen0308: This is a new type of waterproof soil moisture sensor introduced by DFRobot. Compared with the previous version of the soil moisture sensor, it has increased waterproof performance, optimized corrosion resistance, increased plate length and optimized circuit performance. Compared with the resistive sensor, the capacitive soil moisture sensor solves the problem that the resistive sensor is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
  Raspberry Pi 4: The RPi4, a faster version of the awesome Raspberry Pi 2 B ARM Board with 40 pin gpio. Ready for special Raspberry Pi B+ and RPi2 Hat (Hardware attached (on) top)
  Arducam Multi Camera Adapter Module: .Raspberry Pi multi-camera adapter is designed for connecting more than one MIPI camera to a single CSI camera port on the Raspberry Pi board.
  Rasberry Pi NIOR Camera: Camera
  Adafruit BMP388: Bosch has been a leader in barometric pressure sensors, from the BMP085. BMP180, and BMP280... now we've got the next generation, the Adafruit BMP388 Precision Barometric Pressure sensor. As you would expect, this sensor is similar to its earlier versions but even better. The BMP388 has better precision than ever, which makes it excellent for environmental sensing or as a precision altimeter.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
  Adafruit SCD4x: Take a deep breath in...now slowly breathe out. Mmm isn't it wonderful? All that air around us, which we bring into our lungs, extracts oxygen from and then breathes out carbon dioxide. CO2 is essential for life on this planet we call Earth - we and plants take turns using and emitting CO2 in an elegant symbiosis. But it's important to keep that CO2 balanced - you don't want too much around,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
  TM1637: A 4 7-seg display
  LM2596 step down module: LM2596 DC-DC step down power supply module 3 A.
  120V duplex outlet_1: 120V duplex outlet.
  INA 260: Rev. B, add copy
